# Fritzing sketch DIAGRAMA_FISICO_FINAL (saved by Fritzing 0.9.3b)

parts:
  pcb1 = Battery Holders [package=battery-aa]  # not connected
  Placa_Madre1 = Mystery Part - 3 pins [chip_label=? package=THT]  # not connected
  pcb2 = Battery Holders [package=battery-aa]  # not connected
  pcb3 = Battery Holders [package=battery-aa]  # not connected
  J4 = male pin header, 5 pins [form="♂ (male)"]
  J5 = male pin header, 5 pins [form="♂ (male)"]
  J6 = male pin header, 5 pins [form="♂ (male)"]
  J7 = male pin header, 6 pins [form="♂ (male)"]
  J8 = male pin header, 6 pins [form="♂ (male)"]  # not connected
  J9 = male pin header, 6 pins [form="♂ (male)"]
  J10 = male pin header, 6 pins [form="♂ (male)"]  # not connected
  J11 = male pin header, 6 pins [form="♂ (male)"]
  J12 = male pin header, 6 pins [form="♂ (male)"]  # not connected
  J13 = male pin header, 5 pins [form="♂ (male)"]
  J14 = male pin header, 5 pins [form="♂ (male)"]
  J15 = male pin header, 5 pins [form="♂ (male)"]  # not connected
  J16 = male pin header, 3 pins [form="♂ (male)"]  # not connected
  J17 = male pin header, 3 pins [form="♂ (male)"]  # not connected
  J19 = male pin header, 3 pins [form="♂ (male)"]
  J20 = male pin header, 3 pins [form="♂ (male)"]
  J21 = male pin header, 3 pins [form="♂ (male)"]  # not connected
  Componente3 = TE466 [part_number=TE466]
  J22 = Camdenboss CTB0158-2 [part_number=CTB0158-2 package=THT]
  J23 = female pin header, 7 pins [form="♀ (female)"]
  J24 = Camdenboss CTB0158-2 [part_number=CTB0158-2 package=THT]
  J26 = female pin header, 5 pins [form="♀ (female)"]  # not connected
  J27 = female pin header, 6 pins [form="♀ (female)"]  # not connected
  J29 = Camdenboss CTB0158-8 [part_number=CTB0158-8 package=THT]  # not connected
  J25 = female pin header, 5 pins [form="♀ (female)"]
  J28 = Camdenboss CTB0158-8 [part_number=CTB0158-8 package=THT]
  J31 = female pin header, 6 pins [form="♀ (female)"]
  J32 = Camdenboss CTB0158-5 [part_number=CTB0158-5 package=THT]
  J33 = Camdenboss CTB0158-5 [part_number=CTB0158-5 package=THT]
  J34 = Camdenboss CTB0158-5 [part_number=CTB0158-5 package=THT]
  J35 = Camdenboss CTB0158-8 [part_number=CTB0158-8 package=THT]
  J36 = Camdenboss CTB0158-8 [part_number=CTB0158-8 package=THT]
  J37 = female pin header, 6 pins [form="♀ (female)"]
  J38 = female pin header, 6 pins [form="♀ (female)"]
  J39 = female pin header, 5 pins [form="♀ (female)"]
  J40 = female pin header, 5 pins [form="♀ (female)"]
  LED2 = LED - 3mm [color="Red (633nm)" package="3 mm [THT]"]  # not connected
  R1 = Resistor [tolerance=±5% resistance=220 package="2010 [SMD]"]  # not connected
  J18 = male pin header, 3 pins [form="♂ (male)"]
  LED3 = LED - 3mm [color="Red (633nm)" package="3 mm [THT]"]  # not connected
  R2 = Resistor [tolerance=±5% resistance=220 package="2010 [SMD]"]  # not connected
  LED4 = LED - 3mm [color="Red (633nm)" package="3 mm [THT]"]  # not connected
  R3 = Resistor [tolerance=±5% resistance=220 package="2010 [SMD]"]  # not connected
  PCBPWM1 = Battery Holders [package=battery-aa]  # not connected
  J41 = female pin header, 1 pin [form="♀ (female)"]
  AMS1 = AMS1777 5V regulator module
  J42 = Camdenboss CTB0158-3 [part_number=CTB0158-3 package=THT]
  C1 = Film/Foil Capacitor [capacitance=100nF voltage=35V package="5mm [THT, pp]"]
  C2 = Film/Foil Capacitor [capacitance=100nF voltage=35V package="5mm [THT, pp]"]
  R4 = Resistor [tolerance=±5% resistance=220 package="1206 [SMD]"]
  R5 = Resistor [tolerance=±5% resistance=220 package="1206 [SMD]"]
  R6 = Resistor [tolerance=±5% resistance=220 package="1206 [SMD]"]  # not connected
  C3 = Film/Foil Capacitor [capacitance=100nF voltage=35V package="7.5mm [THT, pp]"]  # not connected
  J46 = female pin header, 2 pins [form="♀ (female)"]
  J45 = shrouded pin header, 6 pins [form="♂ (shrouded male)"]
  M5 = Stepper Motor - Unipolar
  J47 = Basic Servo
  SW6 = ToggleSW_Blue1
  SW7 = ToggleSW_Blue1
  SW8 = ToggleSW_Blue1
  SW9 = ToggleSW_Blue1
  SW10 = ToggleSW_Blue1
  M7 = Stepper Motor - Unipolar
  J49 = Camdenboss CTB0158-10 [part_number=CTB0158-10 package=THT]
  J48 = Camdenboss CTB0158-10 [part_number=CTB0158-10 package=THT]
  J50 = Camdenboss CTB0158-10 [part_number=CTB0158-10 package=THT]
  J51 = Camdenboss CTB0158-10 [part_number=CTB0158-10 package=THT]
  J52 = Camdenboss CTB0158-10 [part_number=CTB0158-10 package=THT]
  J53 = Camdenboss CTB0158-10 [part_number=CTB0158-10 package=THT]
  J54 = Camdenboss CTB0158-10 [part_number=CTB0158-10 package=THT]
  J55 = Camdenboss CTB0158-10 [part_number=CTB0158-10 package=THT]
  J56 = Camdenboss CTB0158-2 [part_number=CTB0158-2 package=THT]
  J57 = Camdenboss CTB0158-2 [part_number=CTB0158-2 package=THT]
  J58 = Camdenboss CTB0158-2 [part_number=CTB0158-2 package=THT]
  J60 = Camdenboss CTB0158-10 [part_number=CTB0158-10 package=THT]
  J62 = Camdenboss CTB0158-6 [part_number=CTB0158-6 package=THT]
  J61 = Camdenboss CTB0158-6 [part_number=CTB0158-6 package=THT]
  M8 = Stepper Motor - Unipolar
  J63 = Camdenboss CTB0158-6 [part_number=CTB0158-6 package=THT]
  J64 = Camdenboss CTB0158-6 [part_number=CTB0158-6 package=THT]
  J65 = Camdenboss CTB0158-3 [part_number=CTB0158-3 package=THT]  # not connected
  J65_2 = Camdenboss CTB0158-3 [part_number=CTB0158-3 package=THT]
  J67 = Camdenboss CTB0158-12 [part_number=CTB0158-12 package=THT]
  J66 = Camdenboss CTB0158-12 [part_number=CTB0158-12 package=THT]
  SW11 = ToggleSW_Blue1
  J59 = Camdenboss CTB0158-10 [part_number=CTB0158-10 package=THT]

nets:
  N1: J4.pin1, J40.pin1
  N2: J4.pin2, J40.pin2
  N3: J4.pin3, J40.pin3
  N4: J4.pin5, J40.pin5
  N5: J5.pin1, J25.pin1
  N6: J5.pin2, J25.pin4
  N7: J5.pin3, J25.pin3
  N8: J5.pin4, J25.pin2
  N9: J5.pin5, J25.pin5
  N10: J6.pin1, J39.pin1
  N11: J6.pin2, J39.pin4
  N12: J6.pin3, J39.pin3
  N13: J6.pin4, J39.pin2
  N14: J6.pin5, J39.pin5
  N15: J7.pin1, J31.pin1
  N16: J7.pin2, J31.pin2
  N17: J7.pin3, J31.pin3
  N18: J7.pin6, J31.pin6
  N19: J9.pin2, J38.pin3
  N20: J11.pin1, J37.pin1
  N21: J11.pin2, J37.pin2
  N22: J11.pin3, J37.pin3
  N23: J11.pin6, J37.pin6
  N24: J13.pin4, J45.pin1
  N25: J13.pin5, J45.pin3
  N26: J14.pin1, J46.pin1
  N27: J19.pin2, Componente3.INA, J23.pin5
  N28: J20.pin2, Componente3.INB, J23.pin6
  N29: Componente3.OUTA, J24.pin1
  N30: Componente3.OUTB, J24.pin2
  N31: Componente3.GND, Componente3.SRC_-_GND, Componente3.SRC_-_POS, Componente3.CS, J22.pin1, J22.pin2, J23.pin2, J23.pin4
  N32: Componente3.5V, J23.pin1
  N33: Componente3.EN, J23.pin3
  N34: Componente3.PWM, J23.pin7, J41.pin1
  N35: J22.terminal_1, J58.terminal_2
  N36: J24.terminal_1, J63.terminal_2
  N37: J24.terminal_2, J63.terminal_1
  N38: J28.terminal_1, J49.terminal_3
  N39: J28.terminal_3, J49.terminal_2
  N40: J28.terminal_5, J49.terminal_4
  N41: J28.terminal_6, C1.+, R4.Pin_0, J49.terminal_5
  N42: J28.terminal_7, C1.-, R4.Pin_1, J49.terminal_1
  N43: J32.terminal_1, J49.terminal_6
  N44: J32.terminal_2, J49.terminal_8
  N45: J32.terminal_3, J49.terminal_7
  N46: J32.terminal_4, J49.terminal_10
  N47: J32.terminal_5, J49.terminal_9
  N48: J33.terminal_1, J51.terminal_8, J51.terminal_10, J53.terminal_5
  N49: J33.terminal_2, J53.terminal_2
  N50: J33.terminal_3, J53.terminal_1
  N51: J33.terminal_4, J53.terminal_4
  N52: J33.terminal_5, J53.terminal_3
  N53: J34.terminal_1, J55.terminal_5
  N54: J34.terminal_2, J55.terminal_4
  N55: J34.terminal_3, J55.terminal_3
  N56: J35.terminal_1, J51.terminal_5
  N57: J35.terminal_3, J51.terminal_4
  N58: J35.terminal_5, J51.terminal_6
  N59: J35.terminal_6, C2.+, R5.Pin_0, J51.terminal_7
  N60: J35.terminal_7, C2.-, R5.Pin_1, J51.terminal_3
  N61: J36.terminal_3, J53.terminal_9
  N62: J36.terminal_5, J55.terminal_1
  N63: J36.terminal_6, J55.terminal_2
  N64: J36.terminal_7, J53.terminal_8
  N65: J38.pin1, J18.pin1
  N66: J38.pin6, J18.pin3
  N67: AMS1.VIN+, J57.terminal_1
  N68: AMS1.GND-_(input), J57.terminal_2
  N69: AMS1.VOUT+, J42.pin2
  N70: AMS1.GND-_(output), J42.terminal_1
  N71: J46.pin2, J67.terminal_10
  N72: M5.A, J59.terminal_10
  N73: M5.COMMON_1, J59.terminal_9
  N74: M5.C, J59.terminal_8
  N75: M5.B, J59.terminal_7
  N76: M5.COMMON_2, J59.terminal_6
  N77: M5.D, J59.terminal_5
  N78: J47.gnd, J65_2.terminal_1
  N79: J47.vcc, J65_2.terminal_3
  N80: J47.pulse, J65_2.terminal_2
  N81: SW6.Pin0, J66.terminal_8
  N82: SW6.pin_1, J66.terminal_7
  N83: SW7.Pin0, J66.terminal_10
  N84: SW7.pin_1, J66.terminal_9
  N85: SW8.Pin0, J66.terminal_4
  N86: SW8.pin_1, J66.terminal_3
  N87: SW9.Pin0, J66.terminal_6
  N88: SW9.pin_1, J66.terminal_5
  N89: SW10.Pin0, J66.terminal_12
  N90: SW10.pin_1, J66.terminal_11
  N91: M7.A, J61.terminal_6
  N92: M7.COMMON_1, J61.terminal_5
  N93: M7.C, J61.terminal_4
  N94: M7.B, J61.terminal_3
  N95: M7.COMMON_2, J61.terminal_2
  N96: M7.D, J61.terminal_1
  N97: J48.pin1, J60.terminal_2
  N98: J48.terminal_2, J60.terminal_1
  N99: J48.terminal_3, J52.terminal_9, J54.terminal_1, J54.terminal_7
  N100: J48.terminal_4, J48.terminal_7, J50.terminal_5, J54.terminal_3, J54.terminal_8, J54.terminal_10
  N101: J48.terminal_5, J48.terminal_6
  N102: J48.terminal_8, J60.terminal_6
  N103: J48.terminal_9, J60.terminal_5
  N104: J48.terminal_10, J67.terminal_1
  N105: J50.pin10, J60.terminal_3
  N106: J50.terminal_1, J62.terminal_4
  N107: J50.terminal_2, J62.terminal_3
  N108: J50.terminal_3, J50.terminal_4
  N109: J50.terminal_6, J62.terminal_6
  N110: J50.terminal_7, J62.terminal_5
  N111: J50.terminal_8, J67.terminal_7
  N112: J50.terminal_9, J60.terminal_4
  N113: J51.terminal_9, J53.terminal_6
  N114: J52.terminal_2, J63.terminal_6
  N115: J52.terminal_3, J63.terminal_5
  N116: J52.terminal_4, J67.pin9
  N117: J52.terminal_5, J63.terminal_4
  N118: J52.terminal_6, J63.terminal_3
  N119: J52.terminal_7, J62.terminal_2
  N120: J52.terminal_8, J62.terminal_1
  N121: J54.terminal_2, J54.terminal_4, J54.terminal_9, J67.terminal_8
  N122: J55.terminal_7, J55.terminal_9, J56.terminal_2
  N123: J55.terminal_8, J58.terminal_1
  N124: J55.terminal_10, J56.terminal_1
  N125: M8.A, J64.terminal_6
  N126: M8.COMMON_1, J64.terminal_5
  N127: M8.C, J64.terminal_4
  N128: M8.B, J64.terminal_3
  N129: M8.COMMON_2, J64.terminal_2
  N130: M8.D, J64.terminal_1
  N131: J66.terminal_1, SW11.pin_1
  N132: J66.terminal_2, SW11.Pin0

notes:
  SERVO
  MOTOR 2
  MOTOR 1
  MOTOR 3
  F.C.1
  F.C.2
  F.C.3
  F.C.4
  F.C.5
  FUENTE 5V-10V
  FUENTE 12V
  E GND
  E VCC
  QEA
  QEB
  10V
  GND
  5V
  PWM +
  PWM -
  VCC
  señal
  F.C.6
  +5V
  +10V
  2IN+
  1IN+
  3IN+
  M2
  M1

custom parts:
  Battery Holders: Battery Holders Various common sizes : AA, AAA, 20mm coin cell and 12mm coin cell.
  Mystery Part - 3 pins: A dummy, proxy, ersatz, stand-in part for whatever you want. With 3 pins on a 100 mil inline pin header footprint.
  TE466: Description: This is essentially a ramped up version of our Ardumoto motor driver shield. For this monster shield we've replaced the L298 H-bridge with a pair of VNH2SP30 full-bridge motor drivers. We've also beefed up the support circuitry so this board is capable of driving a pair of high-current motors! The VIN and motor out are pitched for our 5mm screw terminals (not included), making it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
  Battery Holders: Battery Holders Various common sizes : AA, AAA, 20mm coin cell and 12mm coin cell.
  AMS1777 5V regulator module: AMS1777 5V regulator module source : https://github.com/ShenTengTu/fritzing_parts/tree/master/voltage%20regulator/AMS1117_5V_regulator_module
  ToggleSW_Blue1: Generic Tiggle Switch on-off-on
